# Fritzing sketch Arduino電源制御回路-yunシールド (saved by Fritzing 0.9.3b)
perfboards: 1

parts:
  ICSP = male pin header, 3 pins [form="♂ (male)"]  # not connected
  Power_plug = Power plug
  IOA = female pin header, 6 pins [form="♀ (female)"]  # not connected
  DCDC = SeeedStudio-DCDC-POW00900M [package="DIP (Dual Inline) [THT]"]
  IOH = female pin header, 10 pins [form="♀ (female)"]
  IOL = female pin header, 8 pins [form="♀ (female)"]
  J33 = male pin header, 19 pins [form="♂ (male)"]
  J34 = male pin header, 19 pins [form="♂ (male)"]
  Relay = RELAY-G6DN-1A [package=1A]
  U1 = RELAY-G6K [part_number=G6K-2F-Y package=2P]
  Power = female pin header, 8 pins [form="♀ (female)"]
  AE-MOD1 = AE-LXDC55-5V
  X1 = USB Connectors DIP [package=usb-a-s-silk-female]
  S1 = Akizuki slide switch IS-1250

nets:
  GND: Power_plug.GND, DCDC.IN-, DCDC.OUT-, Relay.CIO#1, U1.pin_4, U1.pin_8, Power.pin6, Power.pin7, AE-MOD1.GND, X1.GND
  9V: Power_plug.VCC, Relay.SIO#3, AE-MOD1.IN, S1.pin0, S1.pin3
  N1: DCDC.IN+, Relay.SIO#2
  N2: DCDC.OUT+, X1.VBUS
  N3: IOH.pin1, J33.pin1
  N4: IOH.pin2, J33.pin2
  N5: IOH.pin3, J33.pin3
  N6: IOH.pin4, J33.pin4
  N7: IOH.pin5, J33.pin5
  N8: IOH.pin6, J33.pin6
  N9: IOH.pin7, J33.pin7
  N10: IOH.pin8, J33.pin8
  N11: IOH.pin9, J33.pin9
  N12: IOH.pin10, J33.pin10
  N13: IOL.pin1, J33.pin12
  N14: IOL.pin2, J33.pin13
  N15: IOL.pin3, J33.pin14
  N16: IOL.pin4, J33.pin15
  N17: IOL.pin5, J33.pin16
  N18: IOL.pin6, J33.pin17
  N19: IOL.pin7, J33.pin18
  N20: IOL.pin8, J33.pin19
  N21: J34.pin1, J34.pin2, J34.pin3, J34.pin4, J34.pin5, J34.pin6, J34.pin7, J34.pin8, J34.pin9, J34.pin10, J34.pin11, J34.pin12, J34.pin13, J34.pin14, J34.pin15, J34.pin16, J34.pin17, J34.pin18, J34.pin19, U1.pin_1
  N22: Relay.CIO#0, U1.pin_3
  5V: U1.pin_2, Power.pin5
  N23: Power.pin8, S1.pin1, S1.pin4
  N24: AE-MOD1.OUT, S1.pin2, S1.pin5

custom parts:
  Power plug: 秋月電子通商 AE-DC-POWER-JACK-DIP(通販コードK-05148)とその互換品
  SeeedStudio-DCDC-POW00900M: A DIP stand-in part for whatever IC you want. With 4 pins on a 300mil dual inline package (DIP) footprint.
  RELAY-G6DN-1A: OMRON G6DN-1A
  RELAY-G6K: OMRON G6K
  USB Connectors DIP: USB Connectors AE-USB-A-DIP K-07429
  Akizuki slide switch IS-1250: Akizuki slide switch is-1250 (P-01665)
