# Fritzing sketch Arduino電源制御回路-ブレッドボード (saved by Fritzing 0.9.3b)
breadboards: 2

parts:
  VCC1 = Battery block 9V
  パーツ1 = Arduino Uno (Rev3)
  Raspberry_Pi1 = Raspberry Pi 2
  AE-MOD2 = M-04522
  U1 = RELAY-G6DN-1A [package=1A]
  D1 = SeeedStudio-DCDC-POW00900M [package="DIP (Dual Inline) [THT]"]
  U3 = USB Connectors [package=usb-a-h]
  U4 = RELAY-G6K [part_number=G6K-2F-Y package=2P]

nets:
  GND: VCC1.-, パーツ1.GND, Raspberry_Pi1.GND, AE-MOD2.GND, AE-MOD2.OE, U1.CIO#0, D1.IN-, D1.OUT-, U3.GND, U4.pin_4, U4.pin_8
  9V: VCC1.+, パーツ1.VIN, U1.SIO#2
  N1: パーツ1.D4, AE-MOD2.B0
  N2: パーツ1.D5_PWM, AE-MOD2.B1
  N3: パーツ1.D6_PWM, AE-MOD2.B2
  N4: パーツ1.D7, U4.pin_1
  5V: パーツ1.5V, AE-MOD2.VCCB, U4.pin_2
  3.3V: Raspberry_Pi1.3v3, Raspberry_Pi1.3V3, AE-MOD2.VCCA
  N5: Raspberry_Pi1.GPIO17, AE-MOD2.A2
  N6: Raspberry_Pi1.GPIO27, AE-MOD2.A1
  N7: Raspberry_Pi1.GPIO22, AE-MOD2.A0
  N8: U1.CIO#1, U4.pin_3
  N9: U1.SIO#3, D1.IN+
  N10: D1.OUT+, U3.D+

custom parts:
  M-04522: Akizuki 8bit bi-directional logic level converter M-04522
  RELAY-G6DN-1A: OMRON G6DN-1A
  SeeedStudio-DCDC-POW00900M: A DIP stand-in part for whatever IC you want. With 4 pins on a 300mil dual inline package (DIP) footprint.
  RELAY-G6K: OMRON G6K
