# Fritzing sketch Pi-Arduino相互接続シールド-Pi用 (saved by Fritzing 0.9.3b)
perfboards: 1

parts:
  JP3 = Grove Header 4pin 90 degree direct mount [package="90 degree"]
  JP4 = Grove Header 4pin 90 degree direct mount [package="90 degree"]
  J1 = male pin header, 20 pins [form="♂ (male)"]
  J2 = male pin header, 20 pins [form="♂ (male)"]
  J3 = male pin header, 20 pins [form="♂ (male)"]
  J4 = male pin header, 20 pins [form="♂ (male)"]

nets:
  N1: JP3.1, J2.pin15, J4.pin15
  N2: JP3.2, J2.pin8, J4.pin8
  3.3V: JP3.3, JP4.3, J2.pin1, J4.pin1
  GND: JP3.4, JP4.4, J1.pin3, J3.pin3
  N3: JP4.1, J2.pin6, J4.pin6
  N4: JP4.2, J2.pin7, J4.pin7
  N5: J1.pin1, J3.pin1
  N6: J1.pin2, J3.pin2
  N7: J1.pin4, J3.pin4
  N8: J1.pin5, J3.pin5
  N9: J1.pin6, J3.pin6
  N10: J1.pin7, J3.pin7
  N11: J1.pin8, J3.pin8
  N12: J1.pin9, J3.pin9
  N13: J1.pin10, J3.pin10
  N14: J1.pin11, J3.pin11
  N15: J1.pin12, J3.pin12
  N16: J1.pin13, J3.pin13
  N17: J1.pin14, J3.pin14
  N18: J1.pin15, J3.pin15
  N19: J1.pin16, J3.pin16
  N20: J1.pin17, J3.pin17
  N21: J1.pin18, J3.pin18
  N22: J1.pin19, J3.pin19
  N23: J1.pin20, J3.pin20
  N24: J2.pin2, J4.pin2
  N25: J2.pin3, J4.pin3
  N26: J2.pin4, J4.pin4
  N27: J2.pin5, J4.pin5
  N28: J2.pin9, J4.pin9
  N29: J2.pin10, J4.pin10
  N30: J2.pin11, J4.pin11
  N31: J2.pin12, J4.pin12
  N32: J2.pin13, J4.pin13
  N33: J2.pin14, J4.pin14
  N34: J2.pin16, J4.pin16
  N35: J2.pin17, J4.pin17
  N36: J2.pin18, J4.pin18
  N37: J2.pin19, J4.pin19
  N38: J2.pin20, J4.pin20

custom parts:
  Grove Header 4pin 90 degree direct mount: Header
