# Fritzing sketch Pi-Arduino相互接続シールド-Uno用 (saved by Fritzing 0.9.2b)
perfboards: 1

parts:
  J2 = male pin header, 3 pins [form="♂ (male)"]  # not connected
  J9 = female pin header, 6 pins [form="♀ (female)"]  # not connected
  J10 = female pin header, 8 pins [form="♀ (female)"]
  J11 = female pin header, 8 pins [form="♀ (female)"]
  J12 = female pin header, 10 pins [form="♀ (female)"]
  AE-MOD4 = M-04522
  JP1 = Grove Header 4pin 90 degree direct mount [package="90 degree"]
  JP2 = Grove Header 4pin 90 degree direct mount [package="90 degree"]
  J13 = male pin header, 17 pins [form="♂ (male)"]
  J14 = male pin header, 17 pins [form="♂ (male)"]
  J15 = male pin header, 17 pins [form="♂ (male)"]
  J16 = male pin header, 17 pins [form="♂ (male)"]
  J17 = male pin header, 17 pins [form="♂ (male)"]
  J18 = male pin header, 17 pins [form="♂ (male)"]
  J19 = male pin header, 17 pins [form="♂ (male)"]
  J20 = male pin header, 17 pins [form="♂ (male)"]

nets:
  5V: J10.pin5, AE-MOD4.VCCB
  GND: J10.pin6, J10.pin7, AE-MOD4.GND, AE-MOD4.OE, JP1.4, JP2.4
  N1: J11.pin1, J13.pin12, J15.pin12, J17.pin12, J19.pin12
  N2: J11.pin2, J13.pin13, J15.pin13, J17.pin13, J19.pin13
  N3: J11.pin3, J13.pin14, J15.pin14, J17.pin14, J19.pin14
  N4: J11.pin4, J13.pin15, J15.pin15, J17.pin15, J19.pin15
  N5: J11.pin5, J13.pin16, J15.pin16, J17.pin16, J19.pin16
  N6: J11.pin6, J13.pin17, J15.pin17, J17.pin17, J19.pin17
  N7: J12.pin1, J13.pin1, J15.pin1, J17.pin1, J19.pin1
  N8: J12.pin2, J13.pin2, J15.pin2, J17.pin2, J19.pin2
  N9: J12.pin3, J13.pin3, J15.pin3, J17.pin3, J19.pin3
  N10: J12.pin4, J13.pin4, J15.pin4, J17.pin4, J19.pin4
  N11: J12.pin5, J13.pin5, J15.pin5, J19.pin5
  N12: J12.pin6, J13.pin6, J15.pin6, J17.pin6, J19.pin6
  N13: J12.pin7, J13.pin7, J15.pin7, J17.pin7, J19.pin7
  N14: J12.pin8, J13.pin8, J15.pin8, J17.pin8, J19.pin8
  N15: J12.pin9, J13.pin9, J15.pin9, J17.pin9, J19.pin9
  N16: J12.pin10, J13.pin10, J15.pin10, J17.pin10, J19.pin10
  N17: AE-MOD4.A0, JP2.1
  N18: AE-MOD4.A1, JP2.2
  N19: AE-MOD4.A2, JP1.1
  N20: AE-MOD4.A3, JP1.2
  3.3V: AE-MOD4.VCCA, JP1.3, JP2.3
  N21: AE-MOD4.B0, J20.pin1, J20.pin2, J20.pin3, J20.pin4, J20.pin5, J20.pin6, J20.pin7, J20.pin8, J20.pin9, J20.pin10, J20.pin11, J20.pin12, J20.pin13, J20.pin14, J20.pin15, J20.pin16, J20.pin17
  N22: AE-MOD4.B1, J18.pin1, J18.pin2, J18.pin3, J18.pin4, J18.pin5, J18.pin6, J18.pin7, J18.pin8, J18.pin9, J18.pin10, J18.pin11, J18.pin12, J18.pin13, J18.pin14, J18.pin15, J18.pin16, J18.pin17
  N23: AE-MOD4.B2, J16.pin1, J16.pin2, J16.pin3, J16.pin4, J16.pin5, J16.pin6, J16.pin7, J16.pin8, J16.pin9, J16.pin10, J16.pin11, J16.pin12, J16.pin13, J16.pin14, J16.pin15, J16.pin16, J16.pin17
  N24: AE-MOD4.B3, J14.pin1, J14.pin2, J14.pin3, J14.pin4, J14.pin5, J14.pin6, J14.pin7, J14.pin8, J14.pin9, J14.pin10, J14.pin11, J14.pin12, J14.pin13, J14.pin14, J14.pin15, J14.pin16, J14.pin17

custom parts:
  M-04522: Akizuki 8bit bi-directional logic level converter M-04522
  Grove Header 4pin 90 degree direct mount: Header
