# Fritzing sketch Pi-Arduino相互接続シールド-Uno用シンプル (saved by Fritzing 0.9.3b)
perfboards: 1

parts:
  J9 = female pin header, 6 pins [form="♀ (female)"]  # not connected
  J10 = female pin header, 8 pins [form="♀ (female)"]
  J11 = female pin header, 8 pins [form="♀ (female)"]
  J12 = female pin header, 10 pins [form="♀ (female)"]
  AE-MOD4 = M-04522
  JP1 = Grove Header 4pin 90 degree direct mount [package="90 degree"]
  JP2 = Grove Header 4pin 90 degree direct mount [package="90 degree"]
  J13 = male pin header, 19 pins [form="♂ (male)"]
  J14 = female pin header, 1 pin [form="♀ (female)"]
  J15 = female pin header, 1 pin [form="♀ (female)"]
  J16 = female pin header, 1 pin [form="♀ (female)"]
  J17 = female pin header, 1 pin [form="♀ (female)"]
  S1 = Akizuki slide switch IS-1250

nets:
  N1: J10.pin4, S1.pin2, S1.pin5
  5V: J10.pin5, AE-MOD4.VCCB
  GND: J10.pin6, J10.pin7, AE-MOD4.GND, AE-MOD4.OE, JP1.4, JP2.4
  N2: J11.pin1, J13.pin12
  N3: J11.pin2, J13.pin13
  N4: J11.pin3, J13.pin14
  N5: J11.pin4, J13.pin15
  N6: J11.pin5, J13.pin16
  N7: J11.pin6, J13.pin17
  N8: J11.pin7, J13.pin18
  N9: J11.pin8, J13.pin19
  N10: J12.pin1, J13.pin1
  N11: J12.pin2, J13.pin2
  N12: J12.pin3, J13.pin3
  N13: J12.pin4, J13.pin4
  N14: J12.pin5, J13.pin5
  N15: J12.pin6, J13.pin6
  N16: J12.pin7, J13.pin7
  N17: J12.pin8, J13.pin8
  N18: J12.pin9, J13.pin9
  N19: J12.pin10, J13.pin10
  N20: AE-MOD4.A0, JP2.1
  N21: AE-MOD4.A1, JP2.2
  N22: AE-MOD4.A2, JP1.1
  N23: AE-MOD4.A3, JP1.2
  N24: AE-MOD4.VCCA, S1.pin1, S1.pin4
  N25: AE-MOD4.B0, J17.pin1
  N26: AE-MOD4.B1, J16.pin1
  N27: AE-MOD4.B2, J15.pin1
  N28: AE-MOD4.B3, J14.pin1
  3.3V: JP1.3, JP2.3, S1.pin0, S1.pin3

custom parts:
  M-04522: Akizuki 8bit bi-directional logic level converter M-04522
  Grove Header 4pin 90 degree direct mount: Header
  Akizuki slide switch IS-1250: Akizuki slide switch is-1250 (P-01665)
