# Fritzing sketch Pi-Arduino相互接続シールド-Yun用シンプル (saved by Fritzing 0.9.3b)
perfboards: 1

parts:
  J9 = female pin header, 6 pins [form="♀ (female)"]  # not connected
  J10 = female pin header, 8 pins [form="♀ (female)"]
  J11 = female pin header, 8 pins [form="♀ (female)"]
  J12 = female pin header, 10 pins [form="♀ (female)"]
  JP1 = Grove Header 4pin 90 degree direct mount [package="90 degree"]
  JP2 = Grove Header 4pin 90 degree direct mount [package="90 degree"]
  J13 = male pin header, 19 pins [form="♂ (male)"]
  J14 = female pin header, 1 pin [form="♀ (female)"]
  J15 = female pin header, 1 pin [form="♀ (female)"]
  J16 = female pin header, 1 pin [form="♀ (female)"]
  J17 = female pin header, 1 pin [form="♀ (female)"]
  R1 = Resistor [tolerance=±5% resistance=10k package=THT]
  R2 = Resistor [tolerance=±5% resistance=10k package=THT]
  R3 = Resistor [tolerance=±5% resistance=10k package=THT]
  R4 = Resistor [tolerance=±5% resistance=10k package=THT]
  R5 = Resistor [tolerance=±5% resistance=5.6k package=THT]

nets:
  GND: J10.pin6, J10.pin7, JP1.4, JP2.4, R1.Pin_1, R2.Pin_1, R3.Pin_1, R4.Pin_1
  N1: J11.pin1, J13.pin12
  N2: J11.pin2, J13.pin13
  N3: J11.pin3, J13.pin14
  N4: J11.pin4, J13.pin15
  N5: J11.pin5, J13.pin16
  N6: J11.pin6, J13.pin17
  N7: J11.pin7, J13.pin18
  N8: J11.pin8, J13.pin19
  N9: J12.pin1, J13.pin1
  N10: J12.pin2, J13.pin2
  N11: J12.pin3, J13.pin3
  N12: J12.pin4, J13.pin4
  N13: J12.pin5, J13.pin5
  N14: J12.pin6, J13.pin6
  N15: J12.pin7, J13.pin7
  N16: J12.pin8, J13.pin8
  N17: J12.pin9, J13.pin9
  N18: J12.pin10, J13.pin10
  N19: JP1.1, J15.pin1, R3.Pin_0
  N20: JP1.2, J14.pin1, R2.Pin_0
  N21: JP2.1, J17.pin1, R1.Pin_0
  N22: JP2.2, R4.Pin_0, R5.Pin_1
  N23: J16.pin1, R5.Pin_0

custom parts:
  Grove Header 4pin 90 degree direct mount: Header
