# Fritzing sketch WROOM2-Arduino相互接続シールド-Arduino用 (saved by Fritzing 0.9.3b)
perfboards: 1

parts:
  J2 = male pin header, 3 pins [form="♂ (male)"]  # not connected
  J9 = female pin header, 6 pins [form="♀ (female)"]  # not connected
  J10 = female pin header, 8 pins [form="♀ (female)"]
  J11 = female pin header, 8 pins [form="♀ (female)"]
  J12 = female pin header, 10 pins [form="♀ (female)"]
  JP1 = Grove Header 4pin 90 degree direct mount [package="90 degree"]
  J16 = male pin header, 19 pins [form="♂ (male)"]
  J15 = male pin header, 19 pins [form="♂ (male)"]
  J14 = male pin header, 19 pins [form="♂ (male)"]
  J13 = male pin header, 19 pins [form="♂ (male)"]
  S1 = Akizuki slide switch IS-1250

nets:
  3.3V: J10.pin4, S1.pin0, S1.pin3
  5V: J10.pin5, S1.pin2, S1.pin5
  GND: J10.pin6, J10.pin7, JP1.4
  N1: J11.pin1, J15.pin12, J13.pin12
  N2: J11.pin2, J15.pin13, J13.pin13
  N3: J11.pin3, J15.pin14, J13.pin14
  N4: J11.pin4, J15.pin15, J13.pin15
  N5: J11.pin5, J15.pin16, J13.pin16
  N6: J11.pin6, J15.pin17, J13.pin17
  N7: J11.pin7, J15.pin18, J13.pin18
  N8: J11.pin8, J15.pin19, J13.pin19
  N9: J12.pin1, J15.pin1, J13.pin1
  N10: J12.pin2, J15.pin2, J13.pin2
  N11: J12.pin3, J15.pin3, J13.pin3
  N12: J12.pin4, J15.pin4, J13.pin4
  N13: J12.pin5, J15.pin5, J13.pin5
  N14: J12.pin6, J15.pin6, J13.pin6
  N15: J12.pin7, J15.pin7, J13.pin7
  N16: J12.pin8, J15.pin8, J13.pin8
  N17: J12.pin9, J15.pin9, J13.pin9
  N18: J12.pin10, J15.pin10, J13.pin10
  N19: JP1.1, J16.pin1, J16.pin2, J16.pin3, J16.pin4, J16.pin5, J16.pin6, J16.pin7, J16.pin8, J16.pin9, J16.pin10, J16.pin11, J16.pin12, J16.pin13, J16.pin14, J16.pin15, J16.pin16, J16.pin17, J16.pin18, J16.pin19
  N20: JP1.2, J14.pin1, J14.pin2, J14.pin3, J14.pin4, J14.pin5, J14.pin6, J14.pin7, J14.pin8, J14.pin9, J14.pin10, J14.pin11, J14.pin12, J14.pin13, J14.pin14, J14.pin15, J14.pin16, J14.pin17, J14.pin18, J14.pin19
  N21: JP1.3, S1.pin1, S1.pin4

custom parts:
  Grove Header 4pin 90 degree direct mount: Header
  Akizuki slide switch IS-1250: Akizuki slide switch is-1250 (P-01665)
