# Fritzing sketch WROOM2-Arduino相互接続シールド-Mega用 (saved by Fritzing 0.9.3b)
perfboards: 1

parts:
  J10 = female pin header, 8 pins [form="♀ (female)"]
  J11 = female pin header, 8 pins [form="♀ (female)"]
  J12 = female pin header, 10 pins [form="♀ (female)"]
  JP1 = Grove Header 4pin 90 degree direct mount [package="90 degree"]
  J17 = Arduino R3 6pin male header [package=THT]  # not connected
  J9 = female pin header, 8 pins [form="♀ (female)"]  # not connected
  J18 = female pin header, 8 pins [form="♀ (female)"]  # not connected
  J19 = female pin header, 8 pins [form="♀ (female)"]
  J20 = female pin header, 18 pins [form="♀ (female)"]  # not connected
  J21 = female pin header, 18 pins [form="♀ (female)"]  # not connected
  J13 = male pin header, 28 pins [form="♂ (male)"]
  J22 = female pin header, 1 pin [form="♀ (female)"]
  J23 = female pin header, 1 pin [form="♀ (female)"]

nets:
  3.3V: J10.pin4
  5V: J10.pin5, JP1.3
  GND: J10.pin6, J10.pin7, JP1.4
  N1: J11.pin1, J13.pin12
  N2: J11.pin2, J13.pin13
  N3: J11.pin3, J13.pin14
  N4: J11.pin4, J13.pin15
  N5: J11.pin5, J13.pin16
  N6: J11.pin6, J13.pin17
  N7: J11.pin7, J13.pin18
  N8: J11.pin8, J13.pin19
  N9: J12.pin1, J13.pin1
  N10: J12.pin2, J13.pin2
  N11: J12.pin3, J13.pin3
  N12: J12.pin4, J13.pin4
  N13: J12.pin5, J13.pin5
  N14: J12.pin6, J13.pin6
  N15: J12.pin7, J13.pin7
  N16: J12.pin8, J13.pin8
  N17: J12.pin9, J13.pin9
  N18: J12.pin10, J13.pin10
  N19: JP1.1, J22.pin1
  N20: JP1.2, J23.pin1
  N21: J19.pin1, J13.pin21
  N22: J19.pin2, J13.pin22
  N23: J19.pin3, J13.pin23
  N24: J19.pin4, J13.pin24
  N25: J19.pin5, J13.pin25
  N26: J19.pin6, J13.pin26
  N27: J19.pin7, J13.pin27
  N28: J19.pin8, J13.pin28

custom parts:
  Grove Header 4pin 90 degree direct mount: Header
  Arduino R3 6pin male header: Pin header for arduino R3
