# Fritzing sketch WROOM2-Arduino相互接続シールド-WROOM2用 (saved by Fritzing 0.9.3b)
perfboards: 1

parts:
  J2 = male pin header, 3 pins [form="♂ (male)"]  # not connected
  J9 = female pin header, 6 pins [form="♀ (female)"]  # not connected
  J10 = female pin header, 8 pins [form="♀ (female)"]
  J11 = female pin header, 8 pins [form="♀ (female)"]
  J12 = female pin header, 10 pins [form="♀ (female)"]
  JP1 = Grove Header 4pin 90 degree direct mount [package="90 degree"]
  パーツ1 = Bi-Directional Logic Level Converter [part_number=BOB-12009]
  J18 = Arduino R3 6pin male header [package=THT]
  J16 = male pin header, 19 pins [form="♂ (male)"]
  J15 = male pin header, 19 pins [form="♂ (male)"]
  J14 = male pin header, 19 pins [form="♂ (male)"]
  J13 = male pin header, 19 pins [form="♂ (male)"]

nets:
  3.3V: J10.pin4, パーツ1.LV
  GND: J10.pin6, J10.pin7, JP1.4, パーツ1.GND
  N1: J11.pin1, J15.pin12, J13.pin12
  N2: J11.pin2, J15.pin13, J13.pin13
  N3: J11.pin3, J15.pin14, J13.pin14
  N4: J11.pin4, J15.pin15, J13.pin15
  N5: J11.pin5, J15.pin16, J13.pin16
  N6: J11.pin6, J15.pin17, J13.pin17
  N7: J11.pin7, J15.pin18, J13.pin18
  N8: J11.pin8, J15.pin19, J13.pin19
  N9: J12.pin1, J15.pin1, J13.pin1
  N10: J12.pin2, J15.pin2, J13.pin2
  N11: J12.pin3, J15.pin3, J13.pin3
  N12: J12.pin4, J15.pin4, J13.pin4
  N13: J12.pin5, J15.pin5, J13.pin5
  N14: J12.pin6, J15.pin6, J13.pin6
  N15: J12.pin7, J15.pin7, J13.pin7
  N16: J12.pin8, J15.pin8, J13.pin8
  N17: J12.pin9, J15.pin9, J13.pin9
  N18: J12.pin10, J15.pin10, J13.pin10
  N19: JP1.1, パーツ1.HV1, J18.pin1
  N20: JP1.2, パーツ1.HV2, J18.pin4
  5V: JP1.3, パーツ1.HV
  N21: パーツ1.LV1, J18.pin3
  N22: パーツ1.LV2, J18.pin6
  N23: J18.pin2, J16.pin1, J16.pin2, J16.pin3, J16.pin4, J16.pin5, J16.pin6, J16.pin7, J16.pin8, J16.pin9, J16.pin10, J16.pin11, J16.pin12, J16.pin13, J16.pin14, J16.pin15, J16.pin16, J16.pin17, J16.pin18, J16.pin19
  N24: J18.pin5, J14.pin1, J14.pin2, J14.pin3, J14.pin4, J14.pin5, J14.pin6, J14.pin7, J14.pin8, J14.pin9, J14.pin10, J14.pin11, J14.pin12, J14.pin13, J14.pin14, J14.pin15, J14.pin16, J14.pin17, J14.pin18, J14.pin19

custom parts:
  Grove Header 4pin 90 degree direct mount: Header
  Bi-Directional Logic Level Converter: Description: If you've ever tried to connect a 3.3V device to a 5V system, you know what a challenge it can be. The SparkFun bi-directional logic level converter is a small device that safely steps down 5V signals to 3.3V AND steps up 3.3V to 5V at the same time. This level converter also works with 2.8V and 1.8V devices. What really separates this Logic level converter from our previous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
  Arduino R3 6pin male header: Pin header for arduino R3
