# Fritzing sketch 遠隔ログインPi-Arduino相互接続シールド-Pi用 (saved by Fritzing 0.9.3b)
perfboards: 1

parts:
  JP4 = Grove Header 4pin 90 degree direct mount [package="90 degree"]
  パーツ1 = MM-FT232

nets:
  N1: JP4.1, パーツ1.TXO
  N2: JP4.2, パーツ1.RXI
  3.3V: JP4.3
  GND: JP4.4, パーツ1.GND

custom parts:
  Grove Header 4pin 90 degree direct mount: Header
  MM-FT232: sunhayato MM-FT232
